// Logisim project risk_vee.circ as structural Verilog: 8 circuits, main circuit main
module main (
);

  wire bit_extender_3_out, button_1_out, clock_1_out, console_controller_1_clock_o1,
       console_controller_1_clock_o2, console_controller_1_keyboard_enable, console_controller_1_reset1,
       console_controller_1_reset2, console_controller_1_tty_enable, cpu_1_mem_enable, cpu_1_r_w,
       keyboard_1_avail, memory_decoder_1_io0, memory_decoder_1_io1, memory_decoder_1_memory_enable,
       not_1_out;
  wire [1:0] bit_extender_2_out;
  wire [6:0] console_controller_1_tty_data, keyboard_1_data;
  wire [7:0] console_controller_1_data_out, controlled_buffer_1_out, controlled_buffer_2_out, cpu_1_data_2,
       matrix_controller_1_o0, matrix_controller_1_o1, matrix_controller_1_o2, matrix_controller_1_o3,
       matrix_controller_1_o4, matrix_controller_1_o5, matrix_controller_1_o6, matrix_controller_1_o7;
  wire [23:0] bit_extender_1_out;
  wire [31:0] cpu_1_out_7;

  Clock clock_1 (.out(clock_1_out));
  Button button_1 (.out(button_1_out));
  cpu cpu_1 (
    .clock(clock_1_out), .mem_enable(cpu_1_mem_enable), .r_w(cpu_1_r_w), .data_2(cpu_1_data_2),
    .out_7(cpu_1_out_7), .reset(button_1_out), .data(controlled_buffer_2_out));
  assign controlled_buffer_1_out = not_1_out ? cpu_1_data_2 : 8'bz;  // Controlled_Buffer controlled_buffer_1
  assign controlled_buffer_2_out = cpu_1_r_w ? controlled_buffer_1_out : 8'bz;  // Controlled_Buffer controlled_buffer_2
  Bit_Extender #(.in_width(32), .out_width(24)) bit_extender_1 (.in(cpu_1_out_7), .out(bit_extender_1_out));
  not not_1 (not_1_out, cpu_1_r_w);
  memory_decoder memory_decoder_1 (
    .address(cpu_1_out_7), .enable(cpu_1_mem_enable), .io0(memory_decoder_1_io0), .io1(memory_decoder_1_io1),
    .memory_enable(memory_decoder_1_memory_enable));  // open: io2, io3, io4, io5, io6, io7, io8, io9, io10, io11, io12, io13, io14, io15
  RAM #(.addrWidth(24)) ram_1 (
    .addr(bit_extender_1_out), .data(controlled_buffer_1_out), .sel(memory_decoder_1_memory_enable),
    .clk(clock_1_out), .ld(cpu_1_r_w));  // open: clr
  Bit_Extender #(.in_width(32), .out_width(2)) bit_extender_2 (.in(cpu_1_out_7), .out(bit_extender_2_out));
  Bit_Extender #(.in_width(32), .out_width(1)) bit_extender_3 (.in(cpu_1_out_7), .out(bit_extender_3_out));
  console_controller console_controller_1 (
    .data_in(controlled_buffer_1_out), .enable(memory_decoder_1_io0), .select(bit_extender_2_out),
    .clock(clock_1_out), .keyboard_available(keyboard_1_avail), .keyboard_data(keyboard_1_data),
    .tty_data(console_controller_1_tty_data), .tty_enable(console_controller_1_tty_enable),
    .keyboard_enable(console_controller_1_keyboard_enable), .reset1(console_controller_1_reset1),
    .clock_o2(console_controller_1_clock_o2), .data_out(console_controller_1_data_out),
    .clock_o1(console_controller_1_clock_o1), .reset2(console_controller_1_reset2));  // open: r_w
  TTY #(.rows(25), .cols(80)) tty_1 (
    .data(console_controller_1_tty_data), .clk(console_controller_1_clock_o1),
    .we(console_controller_1_tty_enable), .clr(console_controller_1_reset1));
  Keyboard keyboard_1 (
    .clk(console_controller_1_clock_o2), .re(console_controller_1_keyboard_enable),
    .clr(console_controller_1_reset2), .avail(keyboard_1_avail), .data(keyboard_1_data));
  matrix_controller matrix_controller_1 (
    .data(controlled_buffer_1_out), .clock(clock_1_out), .enable(memory_decoder_1_io1),
    .select(bit_extender_3_out), .o0(matrix_controller_1_o0), .o1(matrix_controller_1_o1),
    .o2(matrix_controller_1_o2), .o3(matrix_controller_1_o3), .o4(matrix_controller_1_o4),
    .o5(matrix_controller_1_o5), .o6(matrix_controller_1_o6), .o7(matrix_controller_1_o7));  // open: reset
  DotMatrix #(.matrixcols(8), .matrixrows(8)) dotmatrix_1 (
    .col0(matrix_controller_1_o7), .col1(matrix_controller_1_o6), .col2(matrix_controller_1_o5),
    .col3(matrix_controller_1_o4), .col4(matrix_controller_1_o3), .col5(matrix_controller_1_o2),
    .col6(matrix_controller_1_o1), .col7(matrix_controller_1_o0));
endmodule

module decoder (
  input  [31:0] ir,
  output [31:0] I,
  output [31:0] S,
  output [31:0] B,
  output [31:0] U,
  output [31:0] J,
  output [4:0] rs1,
  output [4:0] rs2,
  output [4:0] rsd
);


  assign B = {{20{ir[31]}}, ir[7], ir[30:25], ir[11:8], 1'b0};
  assign I = {{21{ir[31]}}, ir[30:20]};
  assign J = {{12{ir[31]}}, ir[19:12], ir[20], ir[30:21], 1'b0};
  assign rs1 = ir[19:15];
  assign rs2 = ir[24:20];
  assign rsd = ir[11:7];
  assign S = {{21{ir[31]}}, ir[30:25], ir[11:7]};
  assign U = {ir[31:12], {12{1'b0}}};

  // Other names for the same wires on the sheet: _8 = ir[8]; _9 = ir[9]; _10 = ir[10]; _11 = ir[11]; _7 = ir[7];
  //   _0 = ir[0]; _1 = ir[1]; _2 = ir[2]; _3 = ir[3]; _4 = ir[4]; _5 = ir[5]; _6 = ir[6]; _21 = ir[21]; _22 = ir[22];
  //   _23 = ir[23]; _24 = ir[24]; _25 = ir[25]; _26 = ir[26]; _27 = ir[27]; _28 = ir[28]; _29 = ir[29]; _30 = ir[30];
  //   _20 = ir[20]; _12 = ir[12]; _13 = ir[13]; _14 = ir[14]; _15 = ir[15]; _16 = ir[16]; _17 = ir[17]; _18 = ir[18];
  //   _19 = ir[19]; _31 = ir[31]
endmodule

module op_decoder (
  input  [31:0] data,
  output [10:0] opcode
);


  assign opcode = {data[30], data[14:12], data[6:0]};

  // Other names for the same wires on the sheet: _7 = data[7]; _8 = data[8]; _9 = data[9]; _10 = data[10];
  //   _11 = data[11]; _15 = data[15]; _16 = data[16]; _17 = data[17]; _18 = data[18]; _19 = data[19]; _20 = data[20];
  //   _21 = data[21]; _22 = data[22]; _23 = data[23]; _24 = data[24]; _25 = data[25]; _26 = data[26]; _27 = data[27];
  //   _28 = data[28]; _29 = data[29]; _31 = data[31]; _0 = data[0]; _1 = data[1]; _2 = data[2]; _3 = data[3];
  //   _4 = data[4]; _5 = data[5]; _6 = data[6]; _12 = data[12]; _13 = data[13]; _14 = data[14]; _30 = data[30]
endmodule

module memory_decoder (
  input  [31:0] address,
  input  enable,
  output io0,
  output io1,
  output io2,
  output io3,
  output io4,
  output io5,
  output io6,
  output io7,
  output io8,
  output io9,
  output io10,
  output io11,
  output io12,
  output io13,
  output io14,
  output io15,
  output memory_enable
);

  wire comparator_1_eq;
  wire [3:0] bit_extender_1_out;
  wire [7:0] bit_extender_2_out;
  wire [31:0] shifter_1_out, shifter_2_out;

  Shifter #(.width(32), .shift("lr")) shifter_1 (.in(address), .\dist (5'b11000), .out(shifter_1_out));
  Shifter #(.width(32), .shift("lr")) shifter_2 (.in(address), .\dist (5'b10100), .out(shifter_2_out));
  Bit_Extender #(.in_width(32), .out_width(4)) bit_extender_1 (.in(shifter_2_out), .out(bit_extender_1_out));
  Bit_Extender #(.in_width(32), .out_width(8)) bit_extender_2 (.in(shifter_1_out), .out(bit_extender_2_out));
  Comparator comparator_1 (.a(bit_extender_2_out), .b({8{1'b1}}), .eq(comparator_1_eq));  // open: gt, lt
  Demultiplexer #(.select(4), .disabled(0)) demultiplexer_1 (
    .out0(io0), .out1(io1), .out2(io2), .out3(io3), .out4(io4), .out5(io5), .out6(io6), .out7(io7),
    .out8(io8), .out9(io9), .out10(io10), .out11(io11), .out12(io12), .out13(io13), .out14(io14),
    .out15(io15), .in(enable), .sel(bit_extender_1_out), .en(comparator_1_eq));
  and and_1 (memory_enable, ~comparator_1_eq, enable);  // AND_Gate
endmodule

module cpu (
  input  clock,
  input  reset,
  input  [7:0] data,
  output mem_enable,
  output r_w,
  output [7:0] data_2,
  output [31:0] out_7
);

  wire alu_a_write, alu_b_write, alu_o_read, and_1_out, and_2_out, and_3_out, and_4_out, and_5_out,
       and_6_out, and_8_out, bitfinder_1_found, compare_latch, d_ff_1_q, decoder_1_out1, decoder_1_out2,
       decoder_1_out3, decoder_1_out4, decoder_1_out5, decoder_1_out6, decoder_1_out7, eq, ge, geu,
       immediate_enable, ir_write, lt, ltu, mem_address_inc, mem_address_write, mem_ar_enable, mem_aw_enable,
       mem_br_enable, mem_bw_enable, mem_cr_enable, mem_cw_enable, mem_data_read, mem_data_write,
       mem_dr_enable, mem_dw_enable, memory_latch_enable, ne, not_4_out, or_2_out, or_3_out, pc_read,
       register_read, register_write;
  wire [0:0] rom_1_data;
  wire [1:0] register_select_select;
  wire [2:0] immediate_select, memory_latch_select, pc_write;
  wire [3:0] alu_select;
  wire [4:0] bit_extender_5_out, decoder_2_rs1, decoder_2_rs2, decoder_2_rsd, register_4_q, register_select;
  wire [5:0] comparator_1_gt;
  wire [7:0] bit_extender_2_out, MEM_Ai_q, MEM_Ao_q, MEM_Bi_q, MEM_Bo_q, MEM_Ci_q, MEM_Co_q, MEM_Di_q,
       MEM_Do_q;
  wire [10:0] op_decoder_1_opcode;
  wire [14:0] bit_extender_8_out, counter_1_q, shifter_4_out;
  wire [15:0] bit_extender_3_out;
  wire [31:0] adder_1_out, adder_2_out, and_7_out, bit_extender_6_out, bit_extender_7_out, decoder_2_b,
       decoder_2_i, decoder_2_j, decoder_2_s, decoder_2_u, ext_b, ext_h, i_data, or_1_out, register_1_q,
       register_2_q, register_3_q, register_5_q, shifter_1_out, shifter_2_out, shifter_3_out,
       subtractor_1_out, xor_1_out;

  Decoder #(.select(3), .enable("false")) decoder_1 (
    .out1(decoder_1_out1), .out2(decoder_1_out2), .out3(decoder_1_out3), .out4(decoder_1_out4),
    .out5(decoder_1_out5), .out6(decoder_1_out6), .out7(decoder_1_out7), .sel(pc_write));  // open: out0
  Register #(.width(32)) register_1 (.D(i_data), .en(alu_a_write), .Q(register_1_q), .clk(clock));  // open: clr
  Register #(.width(32)) register_2 (.D(i_data), .en(alu_b_write), .Q(register_2_q), .clk(clock));  // open: clr
  assign ext_b = {{24{bit_extender_2_out[7]}}, bit_extender_2_out};  // Bit_Extender bit_extender_1
  Bit_Extender #(.in_width(32), .out_width(8)) bit_extender_2 (.in(register_1_q), .out(bit_extender_2_out));
  Bit_Extender #(.in_width(32)) bit_extender_3 (.in(register_1_q), .out(bit_extender_3_out));
  assign ext_h = {{16{bit_extender_3_out[15]}}, bit_extender_3_out};  // Bit_Extender bit_extender_4
  Bit_Extender #(.in_width(32), .out_width(5)) bit_extender_5 (.in(register_2_q), .out(bit_extender_5_out));
  and and_1 (and_1_out, decoder_1_out2, eq);
  and and_2 (and_2_out, decoder_1_out3, lt);
  and and_3 (and_3_out, decoder_1_out4, ltu);
  and and_4 (and_4_out, decoder_1_out5, ne);
  and and_5 (and_5_out, decoder_1_out6, ge);
  and and_6 (and_6_out, decoder_1_out7, geu);
  assign or_1_out = register_1_q | register_2_q;  // OR_Gate or_1, 32 bits wide
  assign and_7_out = register_1_q & register_2_q;  // AND_Gate and_7, 32 bits wide
  or or_2 (or_2_out, decoder_1_out1, and_1_out, and_2_out, and_3_out, and_4_out, and_5_out, and_6_out);
  Adder #(.width(32)) adder_1 (.a(32'h4), .b(register_1_q), .out(adder_1_out));  // open: cin, cout
  Adder #(.width(32)) adder_2 (.a(register_1_q), .b(register_2_q), .out(adder_2_out));  // open: cin, cout
  Subtractor #(.width(32)) subtractor_1 (
    .a(register_1_q), .b(register_2_q), .out(subtractor_1_out));  // open: bin, bout
  assign xor_1_out = register_1_q ^ register_2_q;  // XOR_Gate xor_1, 32 bits wide
  Shifter #(.width(32)) shifter_1 (.in(register_1_q), .\dist (bit_extender_5_out), .out(shifter_1_out));
  Shifter #(.width(32), .shift("lr")) shifter_2 (.in(register_1_q), .\dist (bit_extender_5_out), .out(shifter_2_out));
  Shifter #(.width(32), .shift("ar")) shifter_3 (.in(register_1_q), .\dist (bit_extender_5_out), .out(shifter_3_out));
  Comparator #(.width(32)) comparator_1 (
    .a(register_1_q), .b(register_2_q), .gt(comparator_1_gt[0]), .eq(comparator_1_gt[1]),
    .lt(comparator_1_gt[2]));
  Comparator #(.width(32)) comparator_2 (
    .a(register_1_q), .b(register_2_q), .gt(comparator_1_gt[3]), .eq(comparator_1_gt[4]),
    .lt(comparator_1_gt[5]));
  Register MEM_Ao (.D(i_data[7:0]), .en(mem_data_write), .Q(MEM_Ao_q), .clk(clock));  // open: clr
  assign data = mem_ar_enable ? MEM_Ao_q : 8'bz;  // Controlled_Buffer controlled_buffer_1
  Register MEM_Bo (.D(i_data[15:8]), .en(mem_data_write), .Q(MEM_Bo_q), .clk(clock));  // open: clr
  assign data = mem_br_enable ? MEM_Bo_q : 8'bz;  // Controlled_Buffer controlled_buffer_2
  assign data = mem_cr_enable ? MEM_Co_q : 8'bz;  // Controlled_Buffer controlled_buffer_3
  Register MEM_Co (.D(i_data[23:16]), .en(mem_data_write), .Q(MEM_Co_q), .clk(clock));  // open: clr
  Register MEM_Do (.D(i_data[31:24]), .en(mem_data_write), .Q(MEM_Do_q), .clk(clock));  // open: clr
  assign data = mem_dr_enable ? MEM_Do_q : 8'bz;  // Controlled_Buffer controlled_buffer_4
  assign i_data = pc_read ? register_3_q : 32'bz;  // Controlled_Buffer controlled_buffer_5
  Register #(.width(32)) register_3 (.D(i_data), .en(or_2_out), .Q(register_3_q), .clk(clock), .clr(reset));
  assign bit_extender_6_out = {{31{1'b0}}, comparator_1_gt[5]};  // Bit_Extender bit_extender_6
  assign bit_extender_7_out = {{31{1'b0}}, comparator_1_gt[2]};  // Bit_Extender bit_extender_7
  Multiplexer #(.select(4), .width(32)) multiplexer_1 (
    .in0(adder_1_out), .in1(adder_2_out), .in2(subtractor_1_out), .in3(or_1_out), .in4(and_7_out),
    .in5(xor_1_out), .in6(shifter_1_out), .in7(shifter_2_out), .in8(shifter_3_out), .in9(bit_extender_6_out),
    .in10(bit_extender_7_out), .in11(ext_b), .in12(ext_h), .out(i_data), .sel(alu_select), .en(alu_o_read));  // open: in13, in14, in15
  Register #(.width(6)) register_4 (
    .D(comparator_1_gt), .en(compare_latch), .Q({ltu, register_4_q[4:3], lt, eq, register_4_q[0]}),
    .clk(clock));  // open: clr
  Register MEM_Ai (.D(data), .en(mem_aw_enable), .Q(MEM_Ai_q), .clk(clock), .clr(d_ff_1_q));
  Register MEM_Bi (.D(data), .en(mem_bw_enable), .Q(MEM_Bi_q), .clk(clock), .clr(d_ff_1_q));
  Register MEM_Ci (.D(data), .en(mem_cw_enable), .Q(MEM_Ci_q), .clk(clock), .clr(d_ff_1_q));
  Register MEM_Di (.D(data), .en(mem_dw_enable), .Q(MEM_Di_q), .clk(clock), .clr(d_ff_1_q));
  // Probe on register_write
  // Probe on register_read
  // Probe on pc_write
  // Probe on pc_read
  // Probe on compare_latch
  // Probe on alu_a_write
  // Probe on alu_b_write
  // Probe on alu_o_read
  // Probe on alu_select
  // Probe on mem_data_read
  // Probe on mem_data_write
  // Probe on mem_address_write
  // Probe on mem_address_inc
  // Probe on ir_write
  // Probe on immediate_select
  // Probe on immediate_enable
  not not_1 (ne, eq);
  not not_2 (ge, lt);
  not not_3 (geu, ltu);
  assign i_data = mem_data_read ? {MEM_Di_q, MEM_Ci_q, MEM_Bi_q, MEM_Ai_q} : 32'bz;  // Controlled_Buffer controlled_buffer_6
  D_Flip_Flop d_ff_1 (.clk(clock), .D(mem_data_read), .Q(d_ff_1_q));  // open: Qn, preset, en, reset
  Register #(.width(32)) register_5 (.D(i_data), .en(ir_write), .Q(register_5_q), .clk(clock));  // open: clr
  BitFinder #(.width(5)) bitfinder_1 (.in(register_select), .found(bitfinder_1_found));  // open: index
  and and_8 (and_8_out, bitfinder_1_found, register_write);
  or or_3 (or_3_out, and_8_out, register_read);
  decoder decoder_2 (
    .ir(register_5_q), .I(decoder_2_i), .S(decoder_2_s), .B(decoder_2_b), .U(decoder_2_u), .J(decoder_2_j),
    .rs1(decoder_2_rs1), .rs2(decoder_2_rs2), .rsd(decoder_2_rsd));
  assign bit_extender_8_out = {{4{1'b0}}, op_decoder_1_opcode};  // Bit_Extender bit_extender_8
  op_decoder op_decoder_1 (.data(i_data), .opcode(op_decoder_1_opcode));
  Decoder #(.select(3), .disabled(0)) decoder_3 (
    .out0(mem_dr_enable), .out1(mem_cr_enable), .out2(mem_br_enable), .out3(mem_ar_enable),
    .out4(mem_dw_enable), .out5(mem_cw_enable), .out6(mem_bw_enable), .out7(mem_aw_enable),
    .sel(memory_latch_select), .en(memory_latch_enable));
  Multiplexer #(.select(3), .width(32)) multiplexer_2 (
    .in0(decoder_2_i), .in1(decoder_2_s), .in2(decoder_2_b), .in3(decoder_2_u), .in4(decoder_2_j),
    .out(i_data), .sel(immediate_select), .en(immediate_enable));  // open: in5, in6, in7
  Multiplexer #(.select(2), .width(5), .enable("false")) multiplexer_3 (
    .in0(decoder_2_rs1), .in1(decoder_2_rs2), .in2(decoder_2_rsd), .in3({5{1'b0}}), .out(register_select),
    .sel(register_select_select));
  // Probe on memory_latch_enable
  // Probe on memory_latch_select
  // Probe on register_select_select
  // Probe on register_select
  // Probe on i_data
  // Probe on out_7
  RAM #(.addrWidth(5), .dataWidth(32)) ram_1 (
    .addr(register_select), .data(i_data), .sel(or_3_out), .clk(clock), .ld(register_read), .clr(reset));
  not not_4 (not_4_out, ir_write);
  Shifter #(.width(15)) shifter_4 (.in(bit_extender_8_out), .\dist (4'b0100), .out(shifter_4_out));
  // Probe on mem_enable
  // Probe on r_w
  Counter #(.width(15), .max('h7fff)) counter_1 (
    .load(ir_write), .D(shifter_4_out), .count(not_4_out), .Q(counter_1_q), .clk(clock), .clr(reset));  // open: carry
  ROM #(.addrWidth(15), .dataWidth(32)) rom_1 (
    .addr(counter_1_q),
    .data({register_select_select, memory_latch_select, memory_latch_enable, immediate_enable, immediate_select, ir_write, mem_address_inc, mem_address_write, r_w, mem_enable, mem_data_write, mem_data_read, alu_select, alu_o_read, alu_b_write, alu_a_write, compare_latch, pc_read, pc_write, register_read, register_write, rom_1_data[0]}));  // open: sel
  Counter #(.width(32), .max('hffffffff)) counter_2 (
    .load(mem_address_write), .D(i_data), .count(mem_address_inc), .Q(out_7), .clk(clock));  // open: carry, clr

  assign data_2 = data;

  // Other names for the same wires on the sheet: mem_r_w = r_w; e_addr[31:0] = out_7; e_data[7:0] = data

  // Notes on the sheet:
  //   PROGRAM COUNTER
  //   MEMORY DATA REGISTER(S)
  //   ALU
  //   GP REGISTERS
  //   INSTRUCTION REGISTER/DECODER
  //   contents of rom_1 (hex, n*v repeats v):
  //   80040 3c160000 34160000 2c160000 24160000 208000 10*0 140 408 c0200004 13*0 140 408 c0200004 13*0
  //   104 2000200 80c00 3c060000 8100 80006402 140 408 c0200004 7*0 140 408 c0200004 13*0 140 408 c0200004
  //   13*0 140 408 c0200004 13*0 140 408 c0200004 13*0 140 408 c0200004 13*0 140 408 c0200004 13*0 140 408
  //   c0200004 13*0 140 408 c0200004 13*0 140 408 c0200004 13*0 140 408 c0200004 13*0 140 408 c0200004
  //   13*0 140 408 c0200004 13*0 140 408 c0200004 13*0 140 408 c0200004 13*0 140 408 c0200004 13*0 104
  //   2000200 80000c02 140 408 c0200004 10*0 140 408 c0200004 13*0 140 408 c0200004 13*0 140 408 c0200004
  //   13*0 2c00100 240 80000c00 140 408 c0200004 10*0 140 408 c0200004 13*0 140 408 c0200004 13*0 140 408
  //   c0200004 13*0 140 408 c0200004 13*0 140 408 c0200004 13*0 140 408 c0200004 13*0 140 408 c0200004
  //   13*0 140 408 c0200004 13*0 140 408 c0200004 13*0 140 408 c0200004 13*0 140 408 c0200004 13*0 104
  //   2400200 80c00 40010004 1c020000 140 408 c0200004 8*0 140 408 c0200004 13*0 140 408 c0200004 13*0 140
  //   408 c0200004 13*0 140 408 c0200004 13*0 140 408 c0200004 13*0 140 408 c0200004 13*0 140 408 c0200004
  //   13*0 140 408 c0200004 13*0 140 408 c0200004 13*0 140 408 c0200004 13*0 140 408 c0200004 13*0 140 408
  //   c0200004 13*0 140 408 c0200004 13*0 140 408 c0200004 13*0 140 408 c0200004 13*0 104 40000204
  //   80000c02 140 408 c0200004 10*0 140 408 c0200004 13*0 140 408 c0200004 13*0 140 408 c0200004 13*0
  //   82c00002 140 408 c0200004 12*0 140 408 c0200004 13*0 140 408 c0200004 13*0 140 408 c0200004 13*0 140
  //   408 c0200004 13*0 140 408 c0200004 13*0 140 408 c0200004 13*0 140 408 c0200004 13*0 140 408 c0200004
  //   13*0 140 408 c0200004 13*0 140 408 c0200004 13*0 140 408 c0200004 13*0 140 408 c0200004 13*0 140 408
  //   c0200004 13*0 140 408 c0200004 13*0 140 408 c0200004 13*0 140 408 c0200004 13*0 140 408 c0200004
  //   13*0 140 408 c0200004 13*0 140 408 c0200004 13*0 140 408 c0200004 13*0 140 408 c0200004 13*0 140 408
  //   c0200004 13*0 140 408 c0200004 13*0 140 408 c0200004 13*0 140 408 c0200004 13*0 140 408 c0200004
  //   13*0 140 408 c0200004 13*0 140 408 c0200004 13*0 140 408 c0200004 13*0 140 408 c0200004 13*0 140 408
  //   c0200004 13*0 140 408 c0200004 13*0 140 408 c0200004 13*0 140 408 c0200004 13*0 140 408 c0200004
  //   13*0 140 408 c0200004 13*0 140 408 c0200004 13*0 140 408 c0200004 13*0 140 408 c0200004 13*0 140 408
  //   c0200004 13*0 140 408 c0200004 13*0 140 408 c0200004 13*0 140 408 c0200004 13*0 104 40000204 1c0 408
  //   2800200 c10 c0200004 9*0 140 408 c0200004 13*0 140 408 c0200004 13*0 140 408 c0200004 13*0 140
  //   80000402 104 2000200 c08 c0200004 10*0 140 408 c0200004 13*0 140 408 c0200004 13*0 140 408 c0200004
  //   13*0 140 408 c0200004 13*0 140 408 c0200004 13*0 140 408 c0200004 13*0 140 408 c0200004 13*0 140
  //   3000200 80000402 c08 c0200004 11*0 140 408 c0200004 13*0 140 408 c0200004 13*0 140 408 c0200004 13*0
  //   140 408 c0200004 13*0 140 408 c0200004 13*0 140 408 c0200004 13*0 140 408 c0200004 13*0 140 408
  //   c0200004 13*0 140 408 c0200004 13*0 140 408 c0200004 13*0 140 408 c0200004 13*0 140 408 c0200004
  //   13*0 140 408 c0200004 13*0 140 408 c0200004 13*0 140 408 c0200004 13*0 140 408 c0200004 13*0 140 408
  //   c0200004 13*0 140 408 c0200004 13*0 140 408 c0200004 13*0 104 2000200 80c00 3c160000 34160000 8100
  //   80007402 140 408 c0200004 6*0 140 408 c0200004 13*0 140 408 c0200004 13*0 140 408 c0200004 13*0 140
  //   408 c0200004 13*0 140 408 c0200004 13*0 140 408 c0200004 13*0 140 408 c0200004 13*0 140 408 c0200004
  //   13*0 140 408 c0200004 13*0 140 408 c0200004 13*0 140 408 c0200004 13*0 140 408 c0200004 13*0 140 408
  //   c0200004 13*0 140 408 c0200004 13*0 140 408 c0200004 13*0 104 2000200 80003402 140 408 c0200004 10*0
  //   140 408 c0200004 13*0 140 408 c0200004 13*0 140 408 c0200004 13*0 2c00100 240 80000c00 140 408
  //   c0200004 10*0 140 408 c0200004 13*0 140 408 c0200004 13*0 140 408 c0200004 13*0 140 408 c0200004
  //   13*0 140 408 c0200004 13*0 140 408 c0200004 13*0 140 408 c0200004 13*0 140 408 c0200004 13*0 140 408
  //   c0200004 13*0 140 408 c0200004 13*0 140 408 c0200004 13*0 104 2400200 80c00 40010004 1c120000
  //   14120000 140 408 c0200004 7*0 140 408 c020000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
  //   MEMORY ADDRESS REGISTER
  //   CONTROL UNIT
endmodule

module trans (
  input  in_1,
  input  rw,
  input  in_3,
  output out_4,
  output out_5
);

  wire not_1_out;

  assign out_4 = rw ? in_1 : 1'bz;  // Controlled_Buffer controlled_buffer_1
  not not_1 (not_1_out, rw);
  assign out_5 = not_1_out ? in_3 : 1'bz;  // Controlled_Buffer controlled_buffer_2
endmodule

module console_controller (
  input  [7:0] data_in,
  input  enable,
  input  [1:0] select,
  input  clock,
  input  keyboard_available,
  input  r_w,
  input  [6:0] keyboard_data,
  output [6:0] tty_data,
  output tty_enable,
  output keyboard_enable,
  output reset1,
  output reset2,
  output clock_o1,
  output clock_o2,
  output [7:0] data_out
);

  wire decoder_1_out2;
  wire [7:0] bit_extender_2_out, bit_extender_3_out;

  Decoder #(.select(2), .disabled(0)) decoder_1 (
    .out0(tty_enable), .out1(keyboard_enable), .out2(decoder_1_out2), .out3(reset1), .sel(select), .en(enable));
  Bit_Extender #(.out_width(7)) bit_extender_1 (.in(data_in), .out(tty_data));
  assign bit_extender_2_out = {{7{1'b0}}, keyboard_available};  // Bit_Extender bit_extender_2
  assign data_out = decoder_1_out2 ? bit_extender_2_out : 8'bz;  // Controlled_Buffer controlled_buffer_1
  assign bit_extender_3_out = {{1{1'b0}}, keyboard_data};  // Bit_Extender bit_extender_3
  assign data_out = keyboard_enable ? bit_extender_3_out : 8'bz;  // Controlled_Buffer controlled_buffer_2

  assign clock_o1 = clock;
  assign clock_o2 = clock;
  assign reset2 = reset1;
endmodule

module matrix_controller (
  input  [7:0] data,
  input  clock,
  input  reset,
  input  enable,
  input  select,
  output [7:0] o0,
  output [7:0] o1,
  output [7:0] o2,
  output [7:0] o3,
  output [7:0] o4,
  output [7:0] o5,
  output [7:0] o6,
  output [7:0] o7
);

  wire decoder_1_out0, decoder_1_out1;
  wire [7:0] shift_register_1_q0, shift_register_1_q1, shift_register_1_q2, shift_register_1_q3,
       shift_register_1_q4, shift_register_1_q5, shift_register_1_q6, shift_register_1_q7;

  Decoder #(.disabled(0)) decoder_1 (.out0(decoder_1_out0), .out1(decoder_1_out1), .sel(select), .en(enable));
  Shift_Register #(.width(8)) shift_register_1 (
    .shift(decoder_1_out0), .in(data), .clk(clock), .clr(reset), .q0(shift_register_1_q0),
    .q1(shift_register_1_q1), .q2(shift_register_1_q2), .q3(shift_register_1_q3), .q4(shift_register_1_q4),
    .q5(shift_register_1_q5), .q6(shift_register_1_q6), .q7(shift_register_1_q7));  // open: out, load, d0, d1, d2, d3, d4, d5, d6, d7
  Shift_Register #(.width(8)) shift_register_2 (
    .shift(1'b0), .clk(clock), .load(decoder_1_out1), .clr(reset), .d0(shift_register_1_q0), .q0(o7),
    .d1(shift_register_1_q1), .q1(o6), .d2(shift_register_1_q2), .q2(o5), .d3(shift_register_1_q3), .q3(o4),
    .d4(shift_register_1_q4), .q4(o3), .d5(shift_register_1_q5), .q5(o2), .d6(shift_register_1_q6), .q6(o1),
    .d7(shift_register_1_q7), .q7(o0));  // open: in, out
endmodule
